// Logisim project 8b_cpu_isa2.circ as structural Verilog: 1 circuit, main circuit main
module main (
);

  wire clock_1_out, decoder_1_out0, decoder_1_out1, decoder_1_out2, decoder_1_out3, decoder_1_out4,
       decoder_1_out5, decoder_1_out9, decoder_1_out24, demultiplexer_1_out0, demultiplexer_1_out1,
       demultiplexer_1_out2, demultiplexer_1_out3, demultiplexer_1_out4, demultiplexer_1_out5,
       demultiplexer_1_out6, demultiplexer_1_out7, priority_encoder_1_gs, Reset_out, SingleStep_out;
  wire [1:0] priority_encoder_1_out;
  wire [2:0] ProgramROM_data_2;
  wire [4:0] ProgramROM_data;
  wire [7:0] ACC_q, demultiplexer_2_out0, demultiplexer_2_out1, demultiplexer_2_out2, demultiplexer_2_out3,
       demultiplexer_2_out4, demultiplexer_2_out5, demultiplexer_2_out6, demultiplexer_2_out7,
       multiplexer_1_out, multiplexer_2_out, PC_q, r0_q, r1_q, r2_q, r3_q, r4_q, r5_q, r6_q, r7_q,
       ram_1_dout, STAT_q;

  Clock clock_1 (.out(clock_1_out));
  Button SingleStep (.out(SingleStep_out));
  // Probe on ProgramROM_data
  Button Reset (.out(Reset_out));
  Decoder #(.select(5)) decoder_1 (
    .out0(decoder_1_out0), .out1(decoder_1_out1), .out2(decoder_1_out2), .out3(decoder_1_out3),
    .out4(decoder_1_out4), .out5(decoder_1_out5), .out9(decoder_1_out9), .out24(decoder_1_out24),
    .sel(ProgramROM_data), .en(clock_1_out));  // open: out6, out7, out8, out10, out11, out12, out13, out14, out15, out16, out17, out18, out19, out20, out21, out22, out23, out25, out26, out27, out28, out29, out30, out31
  // Probe on ProgramROM_data_2
  // Probe on decoder_1_out1
  ROM ProgramROM (.addr(PC_q), .data({ProgramROM_data, ProgramROM_data_2}));
  // Probe on decoder_1_out2
  // Probe on decoder_1_out3
  // Probe on {{5{1'b0}}, ProgramROM_data_2}
  Register STAT (.Q(STAT_q));  // open: D, en, clk, clr
  // Probe on {ProgramROM_data, ProgramROM_data_2}
  Register ACC (
    .D({{5{1'b0}}, ProgramROM_data_2}), .en(decoder_1_out1), .clk(decoder_1_out1), .Q(ACC_q), .clr(Reset_out));
  Counter #(.trigger("falling")) PC (
    .clr(Reset_out), .load(decoder_1_out24), .up(1'b1), .count(1'b1), .clk(clock_1_out), .D(ACC_q), .Q(PC_q));  // open: carry
  // Probe on ACC_q
  Multiplexer #(.select(2), .width(8)) multiplexer_1 (
    .in0(ACC_q), .in1(PC_q), .in2(STAT_q), .in3(ram_1_dout), .out(multiplexer_1_out),
    .sel(priority_encoder_1_out));
  Priority_Encoder #(.select(2)) priority_encoder_1 (
    .in0(decoder_1_out9), .in1(decoder_1_out4), .in2(decoder_1_out5), .in3(decoder_1_out2),
    .out(priority_encoder_1_out), .gs(priority_encoder_1_gs));  // open: en_out, en_in
  Demultiplexer #(.select(3)) demultiplexer_1 (
    .out0(demultiplexer_1_out0), .out1(demultiplexer_1_out1), .out2(demultiplexer_1_out2),
    .out3(demultiplexer_1_out3), .out4(demultiplexer_1_out4), .out5(demultiplexer_1_out5),
    .out6(demultiplexer_1_out6), .out7(demultiplexer_1_out7), .in(priority_encoder_1_gs),
    .sel(ProgramROM_data_2));
  // Probe on multiplexer_1_out
  Demultiplexer #(.select(3), .width(8)) demultiplexer_2 (
    .out0(demultiplexer_2_out0), .out1(demultiplexer_2_out1), .out2(demultiplexer_2_out2),
    .out3(demultiplexer_2_out3), .out4(demultiplexer_2_out4), .out5(demultiplexer_2_out5),
    .out6(demultiplexer_2_out6), .out7(demultiplexer_2_out7), .in(multiplexer_1_out), .sel(ProgramROM_data_2));
  // Probe on ACC_q
  RAM ram_1 (
    .addr(ACC_q), .we(decoder_1_out3), .oe(decoder_1_out2), .clk(clock_1_out), .din(multiplexer_2_out),
    .dout(ram_1_dout));
  Register #(.trigger("high")) r0 (
    .D(demultiplexer_2_out0), .en(demultiplexer_1_out0), .clk(demultiplexer_1_out0), .Q(r0_q), .clr(Reset_out));
  Register #(.trigger("high")) r1 (
    .D(demultiplexer_2_out1), .en(demultiplexer_1_out1), .clk(demultiplexer_1_out1), .Q(r1_q), .clr(Reset_out));
  Register #(.trigger("high")) r2 (
    .D(demultiplexer_2_out2), .en(demultiplexer_1_out2), .clk(demultiplexer_1_out2), .Q(r2_q), .clr(Reset_out));
  Register #(.trigger("high")) r3 (
    .D(demultiplexer_2_out3), .en(demultiplexer_1_out3), .clk(demultiplexer_1_out3), .Q(r3_q), .clr(Reset_out));
  Register #(.trigger("high")) r4 (
    .D(demultiplexer_2_out4), .en(demultiplexer_1_out4), .clk(demultiplexer_1_out4), .Q(r4_q), .clr(Reset_out));
  Register #(.trigger("high")) r5 (
    .D(demultiplexer_2_out5), .en(demultiplexer_1_out5), .clk(demultiplexer_1_out5), .Q(r5_q), .clr(Reset_out));
  Register #(.trigger("high")) r6 (
    .D(demultiplexer_2_out6), .en(demultiplexer_1_out6), .clk(demultiplexer_1_out6), .Q(r6_q), .clr(Reset_out));
  Register #(.trigger("high")) r7 (
    .D(demultiplexer_2_out7), .en(demultiplexer_1_out7), .clk(demultiplexer_1_out7), .Q(r7_q), .clr(Reset_out));
  // Probe on demultiplexer_2_out0
  // Probe on demultiplexer_2_out1
  Multiplexer #(.select(3), .width(8)) multiplexer_2 (
    .in0(r0_q), .in1(r1_q), .in2(r2_q), .in3(r3_q), .in4(r4_q), .in5(r5_q), .in6(r6_q), .in7(r7_q),
    .out(multiplexer_2_out), .sel(ProgramROM_data_2));
  // Probe on ram_1_dout
  // Probe on multiplexer_2_out

  // Notes on the sheet:
  //   HALT
  //   LD
  //   GETPC
  //   GETST
  //   LI
  //   ST
  //   GETACC
  //   JMP
  //   contents of ProgramROM (hex, n*v repeats v):
  //   f 10 e 18 49 8 24 29 c0
endmodule
